// Logisim project Final_Project_base-upgrade.circ as structural Verilog: 12 circuits, main circuit 16-bit-ALU
module _16_bit_ALU (
  input  [15:0] A,
  input  [15:0] B,
  input  [1:0] ALU_Op,
  output [15:0] ALU_Out
);

  wire and_1_out;
  wire [15:0] adder_1_out, and_2_out, multiplexer_1_out, not_1_out, or_1_out;

  Multiplexer #(.width(16), .enable("false")) multiplexer_1 (
    .in0(B), .in1(not_1_out), .out(multiplexer_1_out), .sel(and_1_out));
  assign not_1_out = ~B;  // NOT_Gate not_1, 16 bits wide
  and and_1 (and_1_out, ALU_Op[0], ALU_Op[1]);
  Adder #(.width(16)) adder_1 (.a(A), .b(multiplexer_1_out), .out(adder_1_out), .cin(and_1_out));  // open: cout
  assign and_2_out = multiplexer_1_out & A;  // AND_Gate and_2, 16 bits wide
  assign or_1_out = multiplexer_1_out | A;  // OR_Gate or_1, 16 bits wide
  Multiplexer #(.select(2), .width(16), .enable("false")) multiplexer_2 (
    .in0(adder_1_out), .in1(and_2_out), .in2(or_1_out), .in3(adder_1_out), .out(ALU_Out), .sel(ALU_Op));

  // Notes on the sheet:
  //   16 Bit ALU
  //   00 = ADD
  //   01 = AND
  //   10 = OR
  //   11 = SUB
  //   sub not B
  //   sub cin
  //   sub
endmodule

// 0 flag
module _16_bit_ALU_zero_flag (
  input  [15:0] A,
  input  [15:0] B,
  input  [1:0] ALU_Op,
  output Zero_Flag,
  output [15:0] ALU_Out
);

  wire and_1_out;
  wire [15:0] adder_1_out, and_2_out, multiplexer_1_out, not_1_out, or_1_out;

  Multiplexer #(.width(16), .enable("false")) multiplexer_1 (
    .in0(B), .in1(not_1_out), .out(multiplexer_1_out), .sel(and_1_out));
  assign not_1_out = ~B;  // NOT_Gate not_1, 16 bits wide
  and and_1 (and_1_out, ALU_Op[0], ALU_Op[1]);
  Adder #(.width(16)) adder_1 (.a(A), .b(multiplexer_1_out), .out(adder_1_out), .cin(and_1_out));  // open: cout
  assign and_2_out = multiplexer_1_out & A;  // AND_Gate and_2, 16 bits wide
  assign or_1_out = multiplexer_1_out | A;  // OR_Gate or_1, 16 bits wide
  Multiplexer #(.select(2), .width(16), .enable("false")) multiplexer_2 (
    .in0(adder_1_out), .in1(and_2_out), .in2(or_1_out), .in3(adder_1_out), .out(ALU_Out), .sel(ALU_Op));
  Comparator #(.width(16)) comparator_1 (.a({16{1'b0}}), .b(ALU_Out), .eq(Zero_Flag));  // open: gt, lt

  // Notes on the sheet:
  //   16 Bit ALU
  //   00 = ADD
  //   01 = AND
  //   10 = OR
  //   11 = SUB
  //   sub not B
  //   sub cin
  //   sub
endmodule

module _8x16_bit_RF (
  input  [15:0] Data_In,
  input  [2:0] Read_Addr_1,
  input  Write_Enable,
  input  [2:0] Write_Addr,
  input  [2:0] Read_Addr_2,
  input  Clock,
  output [15:0] Read_1_Data,
  output [15:0] Read_2_Data
);

  wire demultiplexer_1_out0, demultiplexer_1_out1, demultiplexer_1_out2, demultiplexer_1_out3,
       demultiplexer_1_out4, demultiplexer_1_out5, demultiplexer_1_out6, demultiplexer_1_out7;
  wire [15:0] register_1_q, register_2_q, register_3_q, register_4_q, register_5_q, register_6_q,
       register_7_q, register_8_q;

  Demultiplexer #(.select(3), .enable("false")) demultiplexer_1 (
    .out0(demultiplexer_1_out0), .out1(demultiplexer_1_out1), .out2(demultiplexer_1_out2),
    .out3(demultiplexer_1_out3), .out4(demultiplexer_1_out4), .out5(demultiplexer_1_out5),
    .out6(demultiplexer_1_out6), .out7(demultiplexer_1_out7), .in(Write_Enable), .sel(Write_Addr));
  Register #(.width(16)) register_1 (
    .D(Data_In), .en(demultiplexer_1_out0), .Q(register_1_q), .clk(Clock));  // open: clr
  Register #(.width(16)) register_2 (
    .D(Data_In), .en(demultiplexer_1_out1), .Q(register_2_q), .clk(Clock));  // open: clr
  Register #(.width(16)) register_3 (
    .D(Data_In), .en(demultiplexer_1_out2), .Q(register_3_q), .clk(Clock));  // open: clr
  Register #(.width(16)) register_4 (
    .D(Data_In), .en(demultiplexer_1_out3), .Q(register_4_q), .clk(Clock));  // open: clr
  Register #(.width(16)) register_5 (
    .D(Data_In), .en(demultiplexer_1_out4), .Q(register_5_q), .clk(Clock));  // open: clr
  Register #(.width(16)) register_6 (
    .D(Data_In), .en(demultiplexer_1_out5), .Q(register_6_q), .clk(Clock));  // open: clr
  Register #(.width(16)) register_7 (
    .D(Data_In), .en(demultiplexer_1_out6), .Q(register_7_q), .clk(Clock));  // open: clr
  Register #(.width(16)) register_8 (
    .D(Data_In), .en(demultiplexer_1_out7), .Q(register_8_q), .clk(Clock));  // open: clr
  Multiplexer #(.select(3), .width(16), .enable("false")) multiplexer_1 (
    .in0(register_1_q), .in1(register_2_q), .in2(register_3_q), .in3(register_4_q), .in4(register_5_q),
    .in5(register_6_q), .in6(register_7_q), .in7(register_8_q), .out(Read_1_Data), .sel(Read_Addr_1));
  Multiplexer #(.select(3), .width(16), .enable("false")) multiplexer_2 (
    .in0(register_1_q), .in1(register_2_q), .in2(register_3_q), .in3(register_4_q), .in4(register_5_q),
    .in5(register_6_q), .in6(register_7_q), .in7(register_8_q), .out(Read_2_Data), .sel(Read_Addr_2));

  // Notes on the sheet:
  //   8x16-bit Register File
  //   R0
  //   R1
  //   R2
  //   R3
  //   R4
  //   R5
  //   R6
  //   R7
endmodule

module ALU_REG_Instruction_16_bit (
  input  [15:0] in_1,
  input  CLK,
  output [15:0] CPU_Op_Out
);

  wire [1:0] multiplexer_2_out;
  wire [15:0] bit_extender_1_out, multiplexer_1_out, n8x16_bit_rf_1_read_1_data, n8x16_bit_rf_1_read_2_data;

  _8x16_bit_RF u_8x16_bit_rf_1 (
    .Data_In(CPU_Op_Out), .Write_Enable(1'b1), .Clock(CLK), .Read_1_Data(n8x16_bit_rf_1_read_1_data),
    .Read_2_Data(n8x16_bit_rf_1_read_2_data), .Write_Addr(in_1[6:4]), .Read_Addr_1(in_1[9:7]),
    .Read_Addr_2(in_1[12:10]));
  assign bit_extender_1_out = {{10{in_1[15]}}, in_1[15:10]};  // Bit_Extender bit_extender_1
  Multiplexer #(.width(16), .enable("false")) multiplexer_1 (
    .in0(n8x16_bit_rf_1_read_2_data), .in1(bit_extender_1_out), .out(multiplexer_1_out), .sel(in_1[0]));
  _16_bit_ALU u_16_bit_alu_1 (
    .A(n8x16_bit_rf_1_read_1_data), .B(multiplexer_1_out), .ALU_Out(CPU_Op_Out), .ALU_Op(multiplexer_2_out));
  Multiplexer #(.width(2), .enable("false")) multiplexer_2 (
    .in0(in_1[15:14]), .in1(in_1[3:2]), .out(multiplexer_2_out), .sel(in_1[0]));

  // Notes on the sheet:
  //   src2
  //   dest
  //   src1
  //   immed data
  //   immed select
  //   ALU op
endmodule

module ALU_with_Mem_16_bit (
  input  [15:0] in_1,
  input  CLK,
  output [15:0] CPU_Op_Out
);

  wire LW, multiplexer_1_out, not_1_out;
  wire [1:0] multiplexer_5_out;
  wire [2:0] multiplexer_2_out;
  wire [15:0] bit_extender_1_out, Din, multiplexer_3_out, multiplexer_4_out, n8x16_bit_rf_1_read_1_data,
       ram_1_data;

  Multiplexer #(.enable("false")) multiplexer_1 (.in0(1'b1), .in1(not_1_out), .out(multiplexer_1_out), .sel(in_1[1]));
  not not_1 (not_1_out, 1'b1);
  Multiplexer #(.width(3), .enable("false")) multiplexer_2 (
    .in0(in_1[12:10]), .in1(in_1[6:4]), .out(multiplexer_2_out), .sel(in_1[0]));
  _8x16_bit_RF u_8x16_bit_rf_1 (
    .Data_In(multiplexer_3_out), .Write_Enable(multiplexer_1_out), .Clock(CLK),
    .Read_1_Data(n8x16_bit_rf_1_read_1_data), .Read_2_Data(Din), .Write_Addr(in_1[6:4]),
    .Read_Addr_1(in_1[9:7]), .Read_Addr_2(multiplexer_2_out));
  assign bit_extender_1_out = {{10{in_1[15]}}, in_1[15:10]};  // Bit_Extender bit_extender_1
  not not_2 (LW, in_1[1]);
  Multiplexer #(.width(16), .enable("false")) multiplexer_3 (
    .in0(CPU_Op_Out), .in1(ram_1_data), .out(multiplexer_3_out), .sel(LW));
  Multiplexer #(.width(16), .enable("false")) multiplexer_4 (
    .in0(Din), .in1(bit_extender_1_out), .out(multiplexer_4_out), .sel(in_1[0]));
  _16_bit_ALU u_16_bit_alu_1 (
    .A(n8x16_bit_rf_1_read_1_data), .B(multiplexer_4_out), .ALU_Out(CPU_Op_Out), .ALU_Op(multiplexer_5_out));
  Multiplexer #(.width(2), .enable("false")) multiplexer_5 (
    .in0(in_1[15:14]), .in1(in_1[3:2]), .out(multiplexer_5_out), .sel(in_1[0]));
  RAM #(.addrWidth(16), .dataWidth(16), .bus("separate")) ram_1 (
    .addr(CPU_Op_Out), .din(Din), .data(ram_1_data), .str(in_1[1]), .sel(1'b1), .clk(CLK), .ld(LW), .clr(1'b0));

  // Notes on the sheet:
  //   src2
  //   dest
  //   src1
  //   immed data
  //   immed select
  //   ALU op
  //   LW
  //   SW
endmodule

module Control_Logic_16_bit_CPU (
  input  R_I,
  input  [2:0] OP_Code,
  input  [2:0] Func,
  output IMM_MUX,
  output SW,
  output WE_MUX,
  output RA2_MUX,
  output BEQ,
  output Jump,
  output BNE,
  output WE,
  output Data_In_MUX,
  output LW,
  output SLT,
  output [1:0] ALU_op,
  output [1:0] Jal_jr
);

  wire and_1_out, and_5_out, nor_1_out, not_1_out, not_2_out, not_3_out, not_4_out, not_5_out, not_6_out,
       or_1_out, or_2_out, or_3_out;
  wire [1:0] multiplexer_1_out, multiplexer_2_out;

  and and_1 (and_1_out, OP_Code[2], OP_Code[0]);
  not not_1 (not_1_out, OP_Code[0]);
  not not_2 (not_2_out, Func[0]);
  and and_2 (Jal_jr[0], not_2_out, Func[1], Func[2]);
  and and_3 (Jal_jr[1], Func[0], Func[1], Func[2]);
  and and_4 (Jump, OP_Code[2], OP_Code[1], not_1_out);
  Multiplexer #(.width(2), .enable("false")) multiplexer_1 (
    .in0(Func[1:0]), .in1(OP_Code[1:0]), .out(multiplexer_1_out), .sel(R_I));
  nor nor_1 (nor_1_out, OP_Code[0], OP_Code[1]);
  and and_5 (and_5_out, OP_Code[0], OP_Code[1]);
  not not_3 (not_3_out, R_I);
  not not_4 (not_4_out, OP_Code[1]);
  and and_6 (SLT, not_3_out, Func[2]);
  and and_7 (SW, nor_1_out, OP_Code[2]);
  and and_8 (BEQ, and_1_out, OP_Code[1]);
  and and_9 (BNE, and_1_out, not_4_out);
  not not_5 (not_5_out, OP_Code[2]);
  and and_10 (Data_In_MUX, not_5_out, and_5_out);
  or or_1 (or_1_out, SLT, BEQ, BNE);
  Multiplexer #(.width(2), .enable("false")) multiplexer_2 (
    .in0(multiplexer_1_out), .in1(2'b11), .out(multiplexer_2_out), .sel(or_1_out));
  or or_2 (or_2_out, Data_In_MUX, SW);
  or or_3 (or_3_out, BEQ, BNE);
  not not_6 (not_6_out, or_3_out);
  Multiplexer #(.width(2), .enable("false")) multiplexer_3 (
    .in0(multiplexer_2_out), .in1(2'b00), .out(ALU_op), .sel(or_2_out));
  and and_11 (IMM_MUX, R_I, not_6_out);

  assign LW = Data_In_MUX;
  assign RA2_MUX = OP_Code[2];
  assign WE = 1'b1;
  assign WE_MUX = OP_Code[2];
endmodule

module CLU_16_bit_upgrade (
  input  R,
  input  [2:0] OPcode,
  input  [2:0] Func,
  output SW,
  output LW,
  output IMM_MUX,
  output WE,
  output RA2_MUX,
  output WE_MUX,
  output DataIn_MUX,
  output [1:0] ALU_OP,
  output slt,
  output beq,
  output bne,
  output j,
  output [1:0] jal_jr
);

  wire [2:0] multiplexer_1_out, multiplexer_2_out;
  wire [15:15] ram_1_data;

  Multiplexer #(.width(3), .enable("false")) multiplexer_1 (
    .in0(3'b000), .in1(OPcode), .out(multiplexer_1_out), .sel(R));
  Multiplexer #(.width(3), .enable("false")) multiplexer_2 (.in0(Func), .in1(3'b000), .out(multiplexer_2_out), .sel(R));
  RAM #(.addrWidth(7), .dataWidth(16), .bus("separate")) ram_1 (
    .addr({R, multiplexer_1_out, multiplexer_2_out}),
    .data({ram_1_data[15], SW, LW, IMM_MUX, WE, RA2_MUX, WE_MUX, DataIn_MUX, ALU_OP, slt, beq, bne, j, jal_jr}));  // open: din, str, sel, clk, ld, clr
endmodule

module ALU_with_Mem_and_Control_16_bit_CPU (
  input  [15:0] in_1,
  input  CLK,
  output [15:0] CPU_Op_Out
);

  wire control_logic_16_bit_cpu_1_lw, control_logic_16_bit_cpu_1_sw, Data_In_MUX, IMM_MUX, multiplexer_1_out,
       not_1_out, RA2_MUX, WE, WE_MUX;
  wire [1:0] OP;
  wire [2:0] multiplexer_2_out;
  wire [15:0] bit_extender_1_out, Din, multiplexer_3_out, multiplexer_4_out, n8x16_bit_rf_1_read_1_data,
       ram_1_data;

  Multiplexer #(.enable("false")) multiplexer_1 (.in0(WE), .in1(not_1_out), .out(multiplexer_1_out), .sel(WE_MUX));
  not not_1 (not_1_out, WE);
  Control_Logic_16_bit_CPU control_logic_16_bit_cpu_1 (
    .R_I(in_1[15]), .OP_Code(in_1[14:12]), .IMM_MUX(IMM_MUX), .SW(control_logic_16_bit_cpu_1_sw),
    .WE_MUX(WE_MUX), .RA2_MUX(RA2_MUX), .WE(WE), .Data_In_MUX(Data_In_MUX),
    .LW(control_logic_16_bit_cpu_1_lw), .ALU_op(OP), .Func(in_1[5:3]));  // open: SLT, BEQ, BNE, Jump, Jal_jr
  // Probe on in_1[5:0]
  Multiplexer #(.width(3), .enable("false")) multiplexer_2 (
    .in0(in_1[2:0]), .in1(in_1[11:9]), .out(multiplexer_2_out), .sel(RA2_MUX));
  // Probe on multiplexer_3_out
  _8x16_bit_RF u_8x16_bit_rf_1 (
    .Data_In(multiplexer_3_out), .Write_Enable(multiplexer_1_out), .Clock(CLK),
    .Read_1_Data(n8x16_bit_rf_1_read_1_data), .Read_2_Data(Din), .Write_Addr(in_1[11:9]),
    .Read_Addr_1(in_1[8:6]), .Read_Addr_2(multiplexer_2_out));
  assign bit_extender_1_out = {{10{in_1[5]}}, in_1[5:0]};  // Bit_Extender bit_extender_1
  Multiplexer #(.width(16), .enable("false")) multiplexer_3 (
    .in0(CPU_Op_Out), .in1(ram_1_data), .out(multiplexer_3_out), .sel(Data_In_MUX));
  Multiplexer #(.width(16), .enable("false")) multiplexer_4 (
    .in0(Din), .in1(bit_extender_1_out), .out(multiplexer_4_out), .sel(IMM_MUX));
  // Probe on multiplexer_4_out
  _16_bit_ALU u_16_bit_alu_1 (.A(n8x16_bit_rf_1_read_1_data), .B(multiplexer_4_out), .ALU_Out(CPU_Op_Out), .ALU_Op(OP));
  RAM #(.addrWidth(16), .dataWidth(16), .bus("separate")) ram_1 (
    .addr(CPU_Op_Out), .din(Din), .data(ram_1_data), .str(control_logic_16_bit_cpu_1_sw), .sel(1'b1),
    .clk(CLK), .ld(control_logic_16_bit_cpu_1_lw), .clr(1'b0));

  // Other names for the same wires on the sheet: Func[2:0] = in_1[5:3]; CLU_Input[3:0] = in_1[15:12]

  // Notes on the sheet:
  //   src2
  //   dest
  //   src1
  //   immed data
endmodule

module PC_16_bit (
  input  CLK,
  input  Reset,
  output [15:0] Output
);

  wire [15:0] adder_1_out, multiplexer_1_out;

  Register #(.width(16)) register_1 (.D(multiplexer_1_out), .en(1'b1), .Q(Output), .clk(CLK), .clr(Reset));
  Adder #(.width(16)) adder_1 (.a(Output), .b(16'h1), .out(adder_1_out));  // open: cin, cout
  Multiplexer #(.width(16), .enable("false")) multiplexer_1 (
    .in0(adder_1_out), .in1({16{1'b0}}), .out(multiplexer_1_out), .sel(Reset));
endmodule

module PC_16_bit_upgrade (
  input  [15:0] in_1,
  input  CLK,
  input  Reset,
  output [15:0] Output
);

  wire [15:0] adder_1_out, multiplexer_1_out, multiplexer_2_out;

  Multiplexer #(.width(16), .enable("false")) multiplexer_1 (
    .in0(multiplexer_2_out), .in1(in_1), .out(multiplexer_1_out), .sel(1'b1));
  Register #(.width(16)) register_1 (.D(multiplexer_1_out), .en(1'b1), .Q(Output), .clk(CLK), .clr(Reset));
  Adder #(.width(16)) adder_1 (.a(Output), .b(16'h1), .out(adder_1_out));  // open: cin, cout
  Multiplexer #(.width(16), .enable("false")) multiplexer_2 (
    .in0(adder_1_out), .in1({16{1'b0}}), .out(multiplexer_2_out), .sel(Reset));
endmodule

module Full_CPU_16_bit__basic (
  input  CLK,
  input  Reset,
  output [15:0] CPU_Op_Out
);

  wire clu_16_bit_upgrade_1_lw, clu_16_bit_upgrade_1_sw, Data_In_MUX, IMM_MUX, multiplexer_1_out, not_1_out,
       RA2_MUX, WE, WE_MUX;
  wire [1:0] OP;
  wire [2:0] Func, multiplexer_2_out;
  wire [3:0] CLU_Input;
  wire [11:3] ram_1_data;
  wire [15:0] bit_extender_1_out, Din, multiplexer_3_out, multiplexer_4_out, n8x16_bit_rf_1_read_1_data,
       pc_16_bit_1_output, ram_2_data;

  PC_16_bit pc_16_bit_1 (.CLK(CLK), .Output(pc_16_bit_1_output), .Reset(Reset));
  RAM #(.addrWidth(16), .dataWidth(16)) ram_1 (
    .addr(pc_16_bit_1_output), .data({CLU_Input, ram_1_data, Func}));  // open: sel, clk, ld, clr
  Multiplexer #(.enable("false")) multiplexer_1 (.in0(WE), .in1(not_1_out), .out(multiplexer_1_out), .sel(WE_MUX));
  not not_1 (not_1_out, WE);
  CLU_16_bit_upgrade clu_16_bit_upgrade_1 (
    .OPcode(CLU_Input[2:0]), .Func(Func), .R(CLU_Input[3]), .SW(clu_16_bit_upgrade_1_sw),
    .LW(clu_16_bit_upgrade_1_lw), .IMM_MUX(IMM_MUX), .WE(WE), .RA2_MUX(RA2_MUX), .WE_MUX(WE_MUX),
    .DataIn_MUX(Data_In_MUX), .ALU_OP(OP));  // open: slt, beq, bne, j, jal_jr
  // Probe on {ram_1_data[5:3], Func}
  Multiplexer #(.width(3), .enable("false")) multiplexer_2 (
    .in0(ram_1_data[5:3]), .in1(ram_1_data[11:9]), .out(multiplexer_2_out), .sel(RA2_MUX));
  // Probe on multiplexer_3_out
  _8x16_bit_RF u_8x16_bit_rf_1 (
    .Data_In(multiplexer_3_out), .Write_Enable(multiplexer_1_out), .Clock(CLK),
    .Read_1_Data(n8x16_bit_rf_1_read_1_data), .Read_2_Data(Din), .Write_Addr(ram_1_data[11:9]),
    .Read_Addr_1(ram_1_data[8:6]), .Read_Addr_2(multiplexer_2_out));
  assign bit_extender_1_out = {{10{ram_1_data[5]}}, {ram_1_data[5:3], Func}};  // Bit_Extender bit_extender_1
  Multiplexer #(.width(16), .enable("false")) multiplexer_3 (
    .in0(CPU_Op_Out), .in1(ram_2_data), .out(multiplexer_3_out), .sel(Data_In_MUX));
  Multiplexer #(.width(16), .enable("false")) multiplexer_4 (
    .in0(Din), .in1(bit_extender_1_out), .out(multiplexer_4_out), .sel(IMM_MUX));
  // Probe on multiplexer_4_out
  _16_bit_ALU u_16_bit_alu_1 (.A(n8x16_bit_rf_1_read_1_data), .B(multiplexer_4_out), .ALU_Out(CPU_Op_Out), .ALU_Op(OP));
  RAM #(.addrWidth(16), .dataWidth(16), .bus("separate")) ram_2 (
    .addr(CPU_Op_Out), .din(Din), .data(ram_2_data), .str(clu_16_bit_upgrade_1_sw), .sel(1'b1), .clk(CLK),
    .ld(clu_16_bit_upgrade_1_lw), .clr(1'b0));

  // Notes on the sheet:
  //   src2
  //   dest
  //   src1
  //   immed data
endmodule

module Full_CPU_16_bit_Upgrade (
  input  Reset,
  input  CLK,
  output [15:0] CPU_Op_Out
);

  wire and_1_out, and_2_out, BEQ, BNE, clu_16_bit_upgrade_1_lw, clu_16_bit_upgrade_1_sw, Data_In_MUX,
       IMM_MUX, Jal, Jal_Jr, Jr, Jump, multiplexer_4_out, n16_bit_alu_zero_flag_1_zero_flag, not_1_out,
       not_2_out, or_2_out, RA2_MUX, SLT, WE, WE_MUX;
  wire [1:0] OP;
  wire [2:0] Func, multiplexer_5_out, multiplexer_6_out, multiplexer_7_out;
  wire [3:0] CLU_Input;
  wire [11:3] ram_1_data;
  wire [15:0] adder_3_out, bit_extender_1_out, bit_extender_2_out, Din, multiplexer_1_out, multiplexer_2_out,
       multiplexer_3_out, multiplexer_8_out, multiplexer_9_out, multiplexer_10_out, multiplexer_11_out,
       multiplexer_12_out, multiplexer_13_out, n8x16_bit_rf_1_read_1_data, PC_1, PC_2,
       pc_16_bit_upgrade_1_output, ram_2_data;

  // Probe on multiplexer_1_out
  Multiplexer #(.width(16), .enable("false")) multiplexer_1 (
    .in0(PC_1), .in1(adder_3_out), .out(multiplexer_1_out), .sel(or_2_out));
  // Probe on bit_extender_1_out
  Adder #(.width(16)) adder_1 (.a(PC_1), .b(16'h1), .out(PC_2));  // open: cin, cout
  Multiplexer #(.width(16), .enable("false")) multiplexer_2 (
    .in0(multiplexer_1_out), .in1(bit_extender_1_out), .out(multiplexer_2_out), .sel(Jump));
  Multiplexer #(.width(16), .enable("false")) multiplexer_3 (
    .in0(multiplexer_2_out), .in1(CPU_Op_Out), .out(multiplexer_3_out), .sel(Jr));
  or or_1 (Jal_Jr, Jal, Jr);
  PC_16_bit_upgrade pc_16_bit_upgrade_1 (
    .CLK(CLK), .Output(pc_16_bit_upgrade_1_output), .Reset(Reset), .in_1(multiplexer_3_out));
  // Probe on pc_16_bit_upgrade_1_output
  not not_1 (not_1_out, WE);
  Adder #(.width(16)) adder_2 (.a(pc_16_bit_upgrade_1_output), .b(16'h1), .out(PC_1));  // open: cin, cout
  // Probe on PC_1
  RAM #(.addrWidth(16), .dataWidth(16)) ram_1 (
    .addr(pc_16_bit_upgrade_1_output), .data({CLU_Input, ram_1_data, Func}));  // open: sel, clk, ld, clr
  Multiplexer #(.enable("false")) multiplexer_4 (.in0(WE), .in1(not_1_out), .out(multiplexer_4_out), .sel(WE_MUX));
  CLU_16_bit_upgrade clu_16_bit_upgrade_1 (
    .OPcode(CLU_Input[2:0]), .Func(Func), .R(CLU_Input[3]), .SW(clu_16_bit_upgrade_1_sw),
    .LW(clu_16_bit_upgrade_1_lw), .IMM_MUX(IMM_MUX), .WE(WE), .RA2_MUX(RA2_MUX), .WE_MUX(WE_MUX),
    .DataIn_MUX(Data_In_MUX), .ALU_OP(OP), .slt(SLT), .beq(BEQ), .bne(BNE), .j(Jump), .jal_jr({Jr, Jal}));
  // Probe on {ram_1_data[5:3], Func}
  assign bit_extender_1_out = {{4{ram_1_data[11]}}, {ram_1_data, Func}};  // Bit_Extender bit_extender_1
  Multiplexer #(.width(3), .enable("false")) multiplexer_5 (
    .in0(ram_1_data[11:9]), .in1(3'b111), .out(multiplexer_5_out), .sel(Jal));
  // Probe on multiplexer_9_out
  Multiplexer #(.width(3), .enable("false")) multiplexer_6 (
    .in0(ram_1_data[8:6]), .in1(3'b111), .out(multiplexer_6_out), .sel(Jr));
  Multiplexer #(.width(3), .enable("false")) multiplexer_7 (
    .in0(ram_1_data[5:3]), .in1(ram_1_data[11:9]), .out(multiplexer_7_out), .sel(RA2_MUX));
  or or_2 (or_2_out, and_1_out, and_2_out);
  // Probe on multiplexer_9_out
  // Probe on n8x16_bit_rf_1_read_1_data
  _8x16_bit_RF u_8x16_bit_rf_1 (
    .Data_In(multiplexer_9_out), .Write_Enable(multiplexer_4_out), .Clock(CLK),
    .Read_1_Data(n8x16_bit_rf_1_read_1_data), .Read_2_Data(Din), .Write_Addr(multiplexer_5_out),
    .Read_Addr_1(multiplexer_6_out), .Read_Addr_2(multiplexer_7_out));
  // Probe on Din
  // Probe on adder_3_out
  and and_1 (and_1_out, BEQ, n16_bit_alu_zero_flag_1_zero_flag);
  and and_2 (and_2_out, BNE, not_2_out);
  // Probe on multiplexer_8_out
  Multiplexer #(.width(16), .enable("false")) multiplexer_8 (
    .in0(Din), .in1(bit_extender_2_out), .out(multiplexer_8_out), .sel(IMM_MUX));
  assign bit_extender_2_out = {{10{ram_1_data[5]}}, {ram_1_data[5:3], Func}};  // Bit_Extender bit_extender_2
  Multiplexer #(.width(16), .enable("false")) multiplexer_9 (
    .in0(multiplexer_12_out), .in1(ram_2_data), .out(multiplexer_9_out), .sel(Data_In_MUX));
  not not_2 (not_2_out, n16_bit_alu_zero_flag_1_zero_flag);
  Multiplexer #(.width(16), .enable("false")) multiplexer_10 (
    .in0(n8x16_bit_rf_1_read_1_data), .in1(PC_2), .out(multiplexer_10_out), .sel(Jal));
  Multiplexer #(.width(16), .enable("false")) multiplexer_11 (
    .in0(multiplexer_8_out), .in1({16{1'b0}}), .out(multiplexer_11_out), .sel(Jal_Jr));
  Adder #(.width(16)) adder_3 (.a(bit_extender_2_out), .b(PC_1), .out(adder_3_out));  // open: cin, cout
  _16_bit_ALU_zero_flag u_16_bit_alu_zero_flag_1 (
    .A(multiplexer_10_out), .B(multiplexer_11_out), .ALU_Out(CPU_Op_Out), .ALU_Op(OP),
    .Zero_Flag(n16_bit_alu_zero_flag_1_zero_flag));
  // Probe on OP
  Multiplexer #(.width(16), .enable("false")) multiplexer_12 (
    .in0(CPU_Op_Out), .in1(multiplexer_13_out), .out(multiplexer_12_out), .sel(SLT));
  Multiplexer #(.width(16), .enable("false")) multiplexer_13 (
    .in0({16{1'b0}}), .in1(16'h1), .out(multiplexer_13_out), .sel(CPU_Op_Out[15]));
  RAM #(.addrWidth(16), .dataWidth(16), .bus("separate")) ram_2 (
    .addr(CPU_Op_Out), .din(Din), .data(ram_2_data), .str(clu_16_bit_upgrade_1_sw), .sel(1'b1), .clk(CLK),
    .ld(clu_16_bit_upgrade_1_lw), .clr(1'b0));

  // Other names for the same wires on the sheet: ra[15:0] = CPU_Op_Out

  // Notes on the sheet:
  //   src1
  //   src2
  //   dest
  //   immed data
endmodule
