// Logisim project Final_Project_base.circ as structural Verilog
module _4_bit_ALU (
  input  [3:0] A,
  input  [3:0] B,
  input  [1:0] ALU_Op,
  output [3:0] ALU_Out
);

  wire and_1_out;
  wire [3:0] adder_1_out, and_2_out, multiplexer_1_out, not_1_out, or_1_out;

  Multiplexer #(.width(4), .enable("false")) multiplexer_1 (
    .in0(B), .in1(not_1_out), .out(multiplexer_1_out), .sel(and_1_out));
  assign not_1_out = ~B;  // NOT_Gate not_1, 4 bits wide
  and and_1 (and_1_out, ALU_Op[0], ALU_Op[1]);
  Adder #(.width(4)) adder_1 (.a(A), .b(multiplexer_1_out), .out(adder_1_out), .cin(and_1_out));  // open: cout
  assign and_2_out = multiplexer_1_out & A;  // AND_Gate and_2, 4 bits wide
  assign or_1_out = multiplexer_1_out | A;  // OR_Gate or_1, 4 bits wide
  Multiplexer #(.select(2), .width(4), .enable("false")) multiplexer_2 (
    .in0(adder_1_out), .in1(and_2_out), .in2(or_1_out), .in3(adder_1_out), .out(ALU_Out), .sel(ALU_Op));

  // Notes on the sheet:
  //   4 Bit ALU
  //   00 = ADD
  //   01 = AND
  //   10 = OR
  //   11 = SUB
  //   sub not B
  //   sub cin
  //   sub
endmodule

module _8x4_bit_Register_File (
  input  [3:0] Data_In,
  input  [2:0] Read_Addr_1,
  input  Write_Enable,
  input  [2:0] Write_Addr,
  input  [2:0] Read_Addr_2,
  input  Clock,
  output [3:0] Read_1_Data,
  output [3:0] Read_2_Data
);

  wire demultiplexer_1_out0, demultiplexer_1_out1, demultiplexer_1_out2, demultiplexer_1_out3,
       demultiplexer_1_out4, demultiplexer_1_out5, demultiplexer_1_out6, demultiplexer_1_out7;
  wire [3:0] register_1_q, register_2_q, register_3_q, register_4_q, register_5_q, register_6_q,
       register_7_q, register_8_q;

  Demultiplexer #(.select(3), .enable("false")) demultiplexer_1 (
    .out0(demultiplexer_1_out0), .out1(demultiplexer_1_out1), .out2(demultiplexer_1_out2),
    .out3(demultiplexer_1_out3), .out4(demultiplexer_1_out4), .out5(demultiplexer_1_out5),
    .out6(demultiplexer_1_out6), .out7(demultiplexer_1_out7), .in(Write_Enable), .sel(Write_Addr));
  Register #(.width(4)) register_1 (
    .D(Data_In), .en(demultiplexer_1_out0), .Q(register_1_q), .clk(Clock));  // open: clr
  Register #(.width(4)) register_2 (
    .D(Data_In), .en(demultiplexer_1_out1), .Q(register_2_q), .clk(Clock));  // open: clr
  Register #(.width(4)) register_3 (
    .D(Data_In), .en(demultiplexer_1_out2), .Q(register_3_q), .clk(Clock));  // open: clr
  Register #(.width(4)) register_4 (
    .D(Data_In), .en(demultiplexer_1_out3), .Q(register_4_q), .clk(Clock));  // open: clr
  Register #(.width(4)) register_5 (
    .D(Data_In), .en(demultiplexer_1_out4), .Q(register_5_q), .clk(Clock));  // open: clr
  Register #(.width(4)) register_6 (
    .D(Data_In), .en(demultiplexer_1_out5), .Q(register_6_q), .clk(Clock));  // open: clr
  Register #(.width(4)) register_7 (
    .D(Data_In), .en(demultiplexer_1_out6), .Q(register_7_q), .clk(Clock));  // open: clr
  Register #(.width(4)) register_8 (
    .D(Data_In), .en(demultiplexer_1_out7), .Q(register_8_q), .clk(Clock));  // open: clr
  Multiplexer #(.select(3), .width(4), .enable("false")) multiplexer_1 (
    .in0(register_1_q), .in1(register_2_q), .in2(register_3_q), .in3(register_4_q), .in4(register_5_q),
    .in5(register_6_q), .in6(register_7_q), .in7(register_8_q), .out(Read_1_Data), .sel(Read_Addr_1));
  Multiplexer #(.select(3), .width(4), .enable("false")) multiplexer_2 (
    .in0(register_1_q), .in1(register_2_q), .in2(register_3_q), .in3(register_4_q), .in4(register_5_q),
    .in5(register_6_q), .in6(register_7_q), .in7(register_8_q), .out(Read_2_Data), .sel(Read_Addr_2));

  // Notes on the sheet:
  //   8x4-bit Register File
  //   R0
  //   R1
  //   R2
  //   R3
  //   R4
  //   R5
  //   R6
  //   R7
endmodule

module ALU_REG_Instruction (
  input  [13:0] dest,
  input  CLK,
  output [3:0] CPU_Op_Out
);

  wire [3:0] bit_extender_1_out, multiplexer_1_out, n8x4_bit_register_file_1_read_1_data,
       n8x4_bit_register_file_1_read_2_data;

  _8x4_bit_Register_File u_8x4_bit_register_file_1 (
    .Read_Addr_2(dest[2:0]), .Data_In(CPU_Op_Out), .Read_1_Data(n8x4_bit_register_file_1_read_1_data),
    .Read_Addr_1(dest[5:3]), .Write_Enable(1'b1), .Write_Addr(dest[8:6]),
    .Read_2_Data(n8x4_bit_register_file_1_read_2_data), .Clock(CLK));
  assign bit_extender_1_out = {{1{dest[2]}}, dest[2:0]};  // Bit_Extender bit_extender_1
  _4_bit_ALU u_4_bit_alu_1 (
    .A(n8x4_bit_register_file_1_read_1_data), .ALU_Out(CPU_Op_Out), .B(multiplexer_1_out), .ALU_Op(dest[10:9]));
  Multiplexer #(.width(4), .enable("false")) multiplexer_1 (
    .in0(n8x4_bit_register_file_1_read_2_data), .in1(bit_extender_1_out), .out(multiplexer_1_out),
    .sel(dest[13]));

  // Notes on the sheet:
  //   op
  //   SW
  //   R/I
  //   LW
  //   src1
  //   dest
  //   src2
  //   src2
  //   dest
  //   src1
  //   immed data
  //   immed select
  //   ALU op
endmodule

module ALU_With_Mem (
  input  [13:0] dest,
  input  CLK,
  output [3:0] CPU_Op_Out
);

  wire multiplexer_1_out, not_1_out;
  wire [2:0] multiplexer_2_out;
  wire [3:0] bit_extender_1_out, Din, multiplexer_3_out, multiplexer_4_out,
       n8x4_bit_register_file_1_read_1_data, ram_1_data;

  not not_1 (not_1_out, 1'b1);
  Multiplexer #(.enable("false")) multiplexer_1 (.in0(1'b1), .in1(not_1_out), .out(multiplexer_1_out), .sel(dest[12]));
  Multiplexer #(.width(3), .enable("false")) multiplexer_2 (
    .in0(dest[2:0]), .in1(dest[8:6]), .out(multiplexer_2_out), .sel(dest[12]));
  _8x4_bit_Register_File u_8x4_bit_register_file_1 (
    .Read_Addr_2(multiplexer_2_out), .Data_In(multiplexer_3_out),
    .Read_1_Data(n8x4_bit_register_file_1_read_1_data), .Read_Addr_1(dest[5:3]),
    .Write_Enable(multiplexer_1_out), .Write_Addr(dest[8:6]), .Read_2_Data(Din), .Clock(CLK));
  assign bit_extender_1_out = {{1{dest[2]}}, dest[2:0]};  // Bit_Extender bit_extender_1
  Multiplexer #(.width(4), .enable("false")) multiplexer_3 (
    .in0(CPU_Op_Out), .in1(ram_1_data), .out(multiplexer_3_out), .sel(dest[11]));
  _4_bit_ALU u_4_bit_alu_1 (
    .A(n8x4_bit_register_file_1_read_1_data), .ALU_Out(CPU_Op_Out), .B(multiplexer_4_out), .ALU_Op(dest[10:9]));
  Multiplexer #(.width(4), .enable("false")) multiplexer_4 (
    .in0(Din), .in1(bit_extender_1_out), .out(multiplexer_4_out), .sel(dest[13]));
  RAM #(.addrWidth(4), .dataWidth(4), .bus("separate")) ram_1 (
    .addr(CPU_Op_Out), .din(Din), .data(ram_1_data), .str(dest[12]), .sel(1'b1), .clk(CLK), .ld(dest[11]),
    .clr(1'b0));

  // Other names for the same wires on the sheet: LW = dest[11]

  // Notes on the sheet:
  //   dest
  //   op
  //   SW
  //   R/I
  //   LW
  //   src2
  //   src1
  //   src1
  //   src2
  //   ALU op
  //   dest
  //   immed data
  //   immed select
  //   LW
  //   SW
endmodule

module Control_Logic (
  input  R_I,
  input  SW,
  input  LW,
  input  [1:0] ALU_OP,
  output IMM_MUX,
  output SW_2,
  output WE_MUX,
  output RA2_MUX,
  output out_9,
  output Data_In_MUX,
  output LW_2,
  output [1:0] ALU_op_2
);


  assign ALU_op_2 = ALU_OP;
  assign Data_In_MUX = LW;
  assign IMM_MUX = R_I;
  assign LW_2 = LW;
  assign out_9 = 1'b1;
  assign RA2_MUX = SW;
  assign SW_2 = SW;
  assign WE_MUX = SW;
endmodule

module ALU_with_Mem_and_Control (
  input  [13:0] dest,
  input  CLK,
  output [3:0] CPU_Op_Out
);

  wire control_logic_1_lw_2, control_logic_1_sw_2, Din_MUX, IMM_MUX, multiplexer_1_out, not_1_out, RA2_MUX,
       WE, WE_MUX;
  wire [1:0] OP;
  wire [2:0] multiplexer_2_out;
  wire [3:0] bit_extender_1_out, Din, multiplexer_3_out, multiplexer_4_out,
       n8x4_bit_register_file_1_read_1_data, ram_1_data;

  not not_1 (not_1_out, WE);
  Multiplexer #(.enable("false")) multiplexer_1 (.in0(WE), .in1(not_1_out), .out(multiplexer_1_out), .sel(WE_MUX));
  Control_Logic control_logic_1 (
    .R_I(dest[13]), .SW(dest[12]), .LW(dest[11]), .ALU_OP(dest[10:9]), .IMM_MUX(IMM_MUX), .WE_MUX(WE_MUX),
    .RA2_MUX(RA2_MUX), .out_9(WE), .Data_In_MUX(Din_MUX), .ALU_op_2(OP), .SW_2(control_logic_1_sw_2),
    .LW_2(control_logic_1_lw_2));
  // Probe on dest[2:0]
  Multiplexer #(.width(3), .enable("false")) multiplexer_2 (
    .in0(dest[2:0]), .in1(dest[8:6]), .out(multiplexer_2_out), .sel(RA2_MUX));
  _8x4_bit_Register_File u_8x4_bit_register_file_1 (
    .Read_Addr_2(multiplexer_2_out), .Data_In(multiplexer_3_out),
    .Read_1_Data(n8x4_bit_register_file_1_read_1_data), .Read_Addr_1(dest[5:3]),
    .Write_Enable(multiplexer_1_out), .Write_Addr(dest[8:6]), .Read_2_Data(Din), .Clock(CLK));
  assign bit_extender_1_out = {{1{dest[2]}}, dest[2:0]};  // Bit_Extender bit_extender_1
  Multiplexer #(.width(4), .enable("false")) multiplexer_3 (
    .in0(CPU_Op_Out), .in1(ram_1_data), .out(multiplexer_3_out), .sel(Din_MUX));
  Multiplexer #(.width(4), .enable("false")) multiplexer_4 (
    .in0(Din), .in1(bit_extender_1_out), .out(multiplexer_4_out), .sel(IMM_MUX));
  _4_bit_ALU u_4_bit_alu_1 (
    .A(n8x4_bit_register_file_1_read_1_data), .ALU_Out(CPU_Op_Out), .B(multiplexer_4_out), .ALU_Op(OP));
  // Probe on multiplexer_4_out
  RAM #(.addrWidth(4), .dataWidth(4), .bus("separate")) ram_1 (
    .addr(CPU_Op_Out), .din(Din), .data(ram_1_data), .str(control_logic_1_sw_2), .sel(1'b1), .clk(CLK),
    .ld(control_logic_1_lw_2), .clr(1'b0));

  // Other names for the same wires on the sheet: CLU_Input[4:0] = dest[13:9]

  // Notes on the sheet:
  //   dest
  //   op
  //   SW
  //   R/I
  //   LW
  //   src1
  //   src2
  //   src1
  //   src2
  //   dest
  //   immed data
  //   immed select
endmodule

module Program_Counter__PC (
  input  CLK,
  input  Reset,
  output [7:0] Output
);

  wire [7:0] adder_1_out, multiplexer_1_out;

  Register register_1 (.D(multiplexer_1_out), .en(1'b1), .Q(Output), .clk(CLK), .clr(Reset));
  Adder adder_1 (.a(Output), .b(8'h1), .out(adder_1_out));  // open: cin, cout
  Multiplexer #(.width(8), .enable("false")) multiplexer_1 (
    .in0(adder_1_out), .in1({8{1'b0}}), .out(multiplexer_1_out), .sel(Reset));
endmodule

module Full_CPU (
  input  CLK,
  input  Reset,
  output [3:0] CPU_Op_Out
);

  wire control_logic_1_lw_2, control_logic_1_sw_2, Din_MUX, IMM_MUX, multiplexer_1_out, not_1_out, RA2_MUX,
       WE, WE_MUX;
  wire [1:0] OP;
  wire [2:0] multiplexer_2_out;
  wire [3:0] bit_extender_1_out, Din, multiplexer_3_out, multiplexer_4_out,
       n8x4_bit_register_file_1_read_1_data, ram_2_data;
  wire [4:0] CLU_Input;
  wire [7:0] program_counter_pc_1_output;
  wire [8:0] ram_1_data;

  // Probe on program_counter_pc_1_output
  Program_Counter__PC program_counter_pc_1 (.CLK(CLK), .Output(program_counter_pc_1_output), .Reset(Reset));
  RAM #(.dataWidth(14)) ram_1 (
    .addr(program_counter_pc_1_output), .data({CLU_Input, ram_1_data}));  // open: sel, clk, ld, clr
  Multiplexer #(.enable("false")) multiplexer_1 (.in0(WE), .in1(not_1_out), .out(multiplexer_1_out), .sel(WE_MUX));
  not not_1 (not_1_out, WE);
  Control_Logic control_logic_1 (
    .R_I(CLU_Input[4]), .SW(CLU_Input[3]), .LW(CLU_Input[2]), .ALU_OP(CLU_Input[1:0]), .IMM_MUX(IMM_MUX),
    .WE_MUX(WE_MUX), .RA2_MUX(RA2_MUX), .out_9(WE), .Data_In_MUX(Din_MUX), .ALU_op_2(OP),
    .SW_2(control_logic_1_sw_2), .LW_2(control_logic_1_lw_2));
  Multiplexer #(.width(3), .enable("false")) multiplexer_2 (
    .in0(ram_1_data[2:0]), .in1(ram_1_data[8:6]), .out(multiplexer_2_out), .sel(RA2_MUX));
  _8x4_bit_Register_File u_8x4_bit_register_file_1 (
    .Read_Addr_2(multiplexer_2_out), .Data_In(multiplexer_3_out),
    .Read_1_Data(n8x4_bit_register_file_1_read_1_data), .Read_Addr_1(ram_1_data[5:3]),
    .Write_Enable(multiplexer_1_out), .Write_Addr(ram_1_data[8:6]), .Read_2_Data(Din), .Clock(CLK));
  assign bit_extender_1_out = {{1{ram_1_data[2]}}, ram_1_data[2:0]};  // Bit_Extender bit_extender_1
  Multiplexer #(.width(4), .enable("false")) multiplexer_3 (
    .in0(CPU_Op_Out), .in1(ram_2_data), .out(multiplexer_3_out), .sel(Din_MUX));
  Multiplexer #(.width(4), .enable("false")) multiplexer_4 (
    .in0(Din), .in1(bit_extender_1_out), .out(multiplexer_4_out), .sel(IMM_MUX));
  _4_bit_ALU u_4_bit_alu_1 (
    .A(n8x4_bit_register_file_1_read_1_data), .ALU_Out(CPU_Op_Out), .B(multiplexer_4_out), .ALU_Op(OP));
  RAM #(.addrWidth(4), .dataWidth(4), .bus("separate")) ram_2 (
    .addr(CPU_Op_Out), .din(Din), .data(ram_2_data), .str(control_logic_1_sw_2), .sel(1'b1), .clk(CLK),
    .ld(control_logic_1_lw_2), .clr(1'b0));

  // Notes on the sheet:
  //   Instruction Memory
  //   src2
  //   dest
  //   src1
  //   immed data
  //   immed select
endmodule

module _16_bit_ALU (
  input  [15:0] A,
  input  [15:0] B,
  input  [1:0] ALU_Op,
  output [15:0] ALU_Out
);

  wire and_1_out;
  wire [15:0] adder_1_out, and_2_out, multiplexer_1_out, not_1_out, or_1_out;

  Multiplexer #(.width(16), .enable("false")) multiplexer_1 (
    .in0(B), .in1(not_1_out), .out(multiplexer_1_out), .sel(and_1_out));
  assign not_1_out = ~B;  // NOT_Gate not_1, 16 bits wide
  and and_1 (and_1_out, ALU_Op[0], ALU_Op[1]);
  Adder #(.width(16)) adder_1 (.a(A), .b(multiplexer_1_out), .out(adder_1_out), .cin(and_1_out));  // open: cout
  assign and_2_out = multiplexer_1_out & A;  // AND_Gate and_2, 16 bits wide
  assign or_1_out = multiplexer_1_out | A;  // OR_Gate or_1, 16 bits wide
  Multiplexer #(.select(2), .width(16), .enable("false")) multiplexer_2 (
    .in0(adder_1_out), .in1(and_2_out), .in2(or_1_out), .in3(adder_1_out), .out(ALU_Out), .sel(ALU_Op));

  // Notes on the sheet:
  //   16 Bit ALU
  //   00 = ADD
  //   01 = AND
  //   10 = OR
  //   11 = SUB
  //   sub not B
  //   sub cin
  //   sub
endmodule

module _8x16_bit_RF (
  input  [15:0] Data_In,
  input  [2:0] Read_Addr_1,
  input  Write_Enable,
  input  [2:0] Write_Addr,
  input  [2:0] Read_Addr_2,
  input  Clock,
  output [15:0] Read_1_Data,
  output [15:0] Read_2_Data
);

  wire demultiplexer_1_out0, demultiplexer_1_out1, demultiplexer_1_out2, demultiplexer_1_out3,
       demultiplexer_1_out4, demultiplexer_1_out5, demultiplexer_1_out6, demultiplexer_1_out7;
  wire [15:0] register_1_q, register_2_q, register_3_q, register_4_q, register_5_q, register_6_q,
       register_7_q, register_8_q;

  Demultiplexer #(.select(3), .enable("false")) demultiplexer_1 (
    .out0(demultiplexer_1_out0), .out1(demultiplexer_1_out1), .out2(demultiplexer_1_out2),
    .out3(demultiplexer_1_out3), .out4(demultiplexer_1_out4), .out5(demultiplexer_1_out5),
    .out6(demultiplexer_1_out6), .out7(demultiplexer_1_out7), .in(Write_Enable), .sel(Write_Addr));
  Register #(.width(16)) register_1 (
    .D(Data_In), .en(demultiplexer_1_out0), .Q(register_1_q), .clk(Clock));  // open: clr
  Register #(.width(16)) register_2 (
    .D(Data_In), .en(demultiplexer_1_out1), .Q(register_2_q), .clk(Clock));  // open: clr
  Register #(.width(16)) register_3 (
    .D(Data_In), .en(demultiplexer_1_out2), .Q(register_3_q), .clk(Clock));  // open: clr
  Register #(.width(16)) register_4 (
    .D(Data_In), .en(demultiplexer_1_out3), .Q(register_4_q), .clk(Clock));  // open: clr
  Register #(.width(16)) register_5 (
    .D(Data_In), .en(demultiplexer_1_out4), .Q(register_5_q), .clk(Clock));  // open: clr
  Register #(.width(16)) register_6 (
    .D(Data_In), .en(demultiplexer_1_out5), .Q(register_6_q), .clk(Clock));  // open: clr
  Register #(.width(16)) register_7 (
    .D(Data_In), .en(demultiplexer_1_out6), .Q(register_7_q), .clk(Clock));  // open: clr
  Register #(.width(16)) register_8 (
    .D(Data_In), .en(demultiplexer_1_out7), .Q(register_8_q), .clk(Clock));  // open: clr
  Multiplexer #(.select(3), .width(16), .enable("false")) multiplexer_1 (
    .in0(register_1_q), .in1(register_2_q), .in2(register_3_q), .in3(register_4_q), .in4(register_5_q),
    .in5(register_6_q), .in6(register_7_q), .in7(register_8_q), .out(Read_1_Data), .sel(Read_Addr_1));
  Multiplexer #(.select(3), .width(16), .enable("false")) multiplexer_2 (
    .in0(register_1_q), .in1(register_2_q), .in2(register_3_q), .in3(register_4_q), .in4(register_5_q),
    .in5(register_6_q), .in6(register_7_q), .in7(register_8_q), .out(Read_2_Data), .sel(Read_Addr_2));

  // Notes on the sheet:
  //   8x16-bit Register File
  //   R0
  //   R1
  //   R2
  //   R3
  //   R4
  //   R5
  //   R6
  //   R7
endmodule

module ALU_REG_Instruction_16_bit (
  input  [15:0] in_1,
  input  CLK,
  output [15:0] CPU_Op_Out
);

  wire [1:0] multiplexer_2_out;
  wire [15:0] bit_extender_1_out, multiplexer_1_out, n8x16_bit_rf_1_read_1_data, n8x16_bit_rf_1_read_2_data;

  _8x16_bit_RF u_8x16_bit_rf_1 (
    .Data_In(CPU_Op_Out), .Write_Enable(1'b1), .Clock(CLK), .Read_1_Data(n8x16_bit_rf_1_read_1_data),
    .Read_2_Data(n8x16_bit_rf_1_read_2_data), .Write_Addr(in_1[6:4]), .Read_Addr_1(in_1[9:7]),
    .Read_Addr_2(in_1[12:10]));
  assign bit_extender_1_out = {{10{in_1[15]}}, in_1[15:10]};  // Bit_Extender bit_extender_1
  Multiplexer #(.width(16), .enable("false")) multiplexer_1 (
    .in0(n8x16_bit_rf_1_read_2_data), .in1(bit_extender_1_out), .out(multiplexer_1_out), .sel(in_1[0]));
  _16_bit_ALU u_16_bit_alu_1 (
    .A(n8x16_bit_rf_1_read_1_data), .B(multiplexer_1_out), .ALU_Out(CPU_Op_Out), .ALU_Op(multiplexer_2_out));
  Multiplexer #(.width(2), .enable("false")) multiplexer_2 (
    .in0(in_1[15:14]), .in1(in_1[3:2]), .out(multiplexer_2_out), .sel(in_1[0]));

  // Notes on the sheet:
  //   src2
  //   dest
  //   src1
  //   immed data
  //   immed select
  //   ALU op
endmodule

module ALU_with_Mem_16_bit (
  input  [15:0] in_1,
  input  CLK,
  output [15:0] CPU_Op_Out
);

  wire LW, multiplexer_1_out, not_1_out;
  wire [1:0] multiplexer_5_out;
  wire [2:0] multiplexer_2_out;
  wire [15:0] bit_extender_1_out, Din, multiplexer_3_out, multiplexer_4_out, n8x16_bit_rf_1_read_1_data,
       ram_1_data;

  Multiplexer #(.enable("false")) multiplexer_1 (.in0(1'b1), .in1(not_1_out), .out(multiplexer_1_out), .sel(in_1[1]));
  not not_1 (not_1_out, 1'b1);
  Multiplexer #(.width(3), .enable("false")) multiplexer_2 (
    .in0(in_1[12:10]), .in1(in_1[6:4]), .out(multiplexer_2_out), .sel(in_1[0]));
  _8x16_bit_RF u_8x16_bit_rf_1 (
    .Data_In(multiplexer_3_out), .Write_Enable(multiplexer_1_out), .Clock(CLK),
    .Read_1_Data(n8x16_bit_rf_1_read_1_data), .Read_2_Data(Din), .Write_Addr(in_1[6:4]),
    .Read_Addr_1(in_1[9:7]), .Read_Addr_2(multiplexer_2_out));
  assign bit_extender_1_out = {{10{in_1[15]}}, in_1[15:10]};  // Bit_Extender bit_extender_1
  not not_2 (LW, in_1[1]);
  Multiplexer #(.width(16), .enable("false")) multiplexer_3 (
    .in0(CPU_Op_Out), .in1(ram_1_data), .out(multiplexer_3_out), .sel(LW));
  Multiplexer #(.width(16), .enable("false")) multiplexer_4 (
    .in0(Din), .in1(bit_extender_1_out), .out(multiplexer_4_out), .sel(in_1[0]));
  _16_bit_ALU u_16_bit_alu_1 (
    .A(n8x16_bit_rf_1_read_1_data), .B(multiplexer_4_out), .ALU_Out(CPU_Op_Out), .ALU_Op(multiplexer_5_out));
  Multiplexer #(.width(2), .enable("false")) multiplexer_5 (
    .in0(in_1[15:14]), .in1(in_1[3:2]), .out(multiplexer_5_out), .sel(in_1[0]));
  RAM #(.addrWidth(16), .dataWidth(16), .bus("separate")) ram_1 (
    .addr(CPU_Op_Out), .din(Din), .data(ram_1_data), .str(in_1[1]), .sel(1'b1), .clk(CLK), .ld(LW), .clr(1'b0));

  // Notes on the sheet:
  //   src2
  //   dest
  //   src1
  //   immed data
  //   immed select
  //   ALU op
  //   LW
  //   SW
endmodule

module Control_Logic_16_bit_CPU (
  input  R_I,
  input  SW_LW,
  input  [2:0] Func,
  input  [1:0] ALU_OP,
  output IMM_MUX,
  output SW,
  output WE_MUX,
  output RA2_MUX,
  output out_9,
  output Data_In_MUX,
  output LW,
  output SLT,
  output [1:0] ALU_op_2
);

  wire and_1_out, nor_1_out, not_1_out;

  Multiplexer #(.width(2), .enable("false")) multiplexer_1 (.in0(Func[2:1]), .in1(ALU_OP), .out(ALU_op_2), .sel(R_I));
  nor nor_1 (nor_1_out, ALU_OP[0], ALU_OP[1]);
  not not_1 (not_1_out, SW_LW);
  and and_1 (and_1_out, ALU_OP[0], ALU_OP[1]);
  and and_2 (SW, nor_1_out, SW_LW);
  and and_3 (Data_In_MUX, not_1_out, and_1_out);

  assign IMM_MUX = R_I;
  assign LW = Data_In_MUX;
  assign out_9 = 1'b1;
  assign RA2_MUX = SW_LW;
  assign SLT = Func[0];
  assign WE_MUX = SW_LW;
endmodule

module ALU_with_Mem_and_Control_16_bit_CPU (
  input  [15:0] in_1,
  input  CLK,
  output [15:0] CPU_Op_Out
);

  wire control_logic_16_bit_cpu_1_lw, control_logic_16_bit_cpu_1_slt, control_logic_16_bit_cpu_1_sw,
       Data_In_MUX, IMM_MUX, multiplexer_1_out, not_1_out, RA2_MUX, WE, WE_MUX;
  wire [1:0] OP;
  wire [2:0] multiplexer_2_out;
  wire [15:0] bit_extender_1_out, Din, multiplexer_3_out, multiplexer_4_out, n8x16_bit_rf_1_read_1_data,
       ram_1_data;

  Multiplexer #(.enable("false")) multiplexer_1 (.in0(WE), .in1(not_1_out), .out(multiplexer_1_out), .sel(WE_MUX));
  not not_1 (not_1_out, WE);
  Control_Logic_16_bit_CPU control_logic_16_bit_cpu_1 (
    .R_I(in_1[15]), .SW_LW(in_1[14]), .ALU_OP(in_1[13:12]), .IMM_MUX(IMM_MUX),
    .SW(control_logic_16_bit_cpu_1_sw), .WE_MUX(WE_MUX), .RA2_MUX(RA2_MUX), .out_9(WE),
    .Data_In_MUX(Data_In_MUX), .LW(control_logic_16_bit_cpu_1_lw), .ALU_op_2(OP), .Func(in_1[5:3]),
    .SLT(control_logic_16_bit_cpu_1_slt));
  // Probe on in_1[5:0]
  Multiplexer #(.width(3), .enable("false")) multiplexer_2 (
    .in0(in_1[2:0]), .in1(in_1[11:9]), .out(multiplexer_2_out), .sel(RA2_MUX));
  // Probe on multiplexer_3_out
  _8x16_bit_RF u_8x16_bit_rf_1 (
    .Data_In(multiplexer_3_out), .Write_Enable(multiplexer_1_out), .Clock(CLK),
    .Read_1_Data(n8x16_bit_rf_1_read_1_data), .Read_2_Data(Din), .Write_Addr(in_1[11:9]),
    .Read_Addr_1(in_1[8:6]), .Read_Addr_2(multiplexer_2_out));
  assign bit_extender_1_out = {{10{in_1[5]}}, in_1[5:0]};  // Bit_Extender bit_extender_1
  Multiplexer #(.width(16), .enable("false")) multiplexer_3 (
    .in0(CPU_Op_Out), .in1(ram_1_data), .out(multiplexer_3_out), .sel(Data_In_MUX));
  Multiplexer #(.width(16), .enable("false")) multiplexer_4 (
    .in0(Din), .in1(bit_extender_1_out), .out(multiplexer_4_out), .sel(IMM_MUX));
  // Probe on multiplexer_4_out
  _16_bit_ALU u_16_bit_alu_1 (.A(n8x16_bit_rf_1_read_1_data), .B(multiplexer_4_out), .ALU_Out(CPU_Op_Out), .ALU_Op(OP));
  RAM #(.addrWidth(16), .dataWidth(16), .bus("separate")) ram_1 (
    .addr(CPU_Op_Out), .din(Din), .data(ram_1_data), .str(control_logic_16_bit_cpu_1_sw), .sel(1'b1),
    .clk(CLK), .ld(control_logic_16_bit_cpu_1_lw), .clr(1'b0));

  // Other names for the same wires on the sheet: Func[2:0] = in_1[5:3]; CLU_Input[3:0] = in_1[15:12]

  // Notes on the sheet:
  //   src2
  //   dest
  //   src1
  //   immed data
endmodule

module PC_16_bit (
  input  CLK,
  input  Reset,
  output [15:0] Output
);

  wire [15:0] adder_1_out, multiplexer_1_out;

  Register #(.width(16)) register_1 (.D(multiplexer_1_out), .en(1'b1), .Q(Output), .clk(CLK), .clr(Reset));
  Adder #(.width(16)) adder_1 (.a(Output), .b(16'h1), .out(adder_1_out));  // open: cin, cout
  Multiplexer #(.width(16), .enable("false")) multiplexer_1 (
    .in0(adder_1_out), .in1({16{1'b0}}), .out(multiplexer_1_out), .sel(Reset));
endmodule

module Full_CPU_16_bit__basic (
  input  CLK,
  input  Reset,
  output [15:0] CPU_Op_Out
);

  wire control_logic_16_bit_cpu_1_lw, control_logic_16_bit_cpu_1_sw, Data_In_MUX, IMM_MUX, multiplexer_1_out,
       not_1_out, RA2_MUX, WE, WE_MUX;
  wire [1:0] OP;
  wire [2:0] Func, multiplexer_2_out;
  wire [3:0] CLU_Input;
  wire [11:0] ram_1_data;
  wire [15:0] bit_extender_1_out, Din, multiplexer_3_out, multiplexer_4_out, n8x16_bit_rf_1_read_1_data,
       pc_16_bit_1_output, ram_2_data;

  PC_16_bit pc_16_bit_1 (.CLK(CLK), .Output(pc_16_bit_1_output), .Reset(Reset));
  RAM #(.addrWidth(16), .dataWidth(16)) ram_1 (
    .addr(pc_16_bit_1_output), .data({CLU_Input, ram_1_data[11:6], Func, ram_1_data[2:0]}));  // open: sel, clk, ld, clr
  Multiplexer #(.enable("false")) multiplexer_1 (.in0(WE), .in1(not_1_out), .out(multiplexer_1_out), .sel(WE_MUX));
  not not_1 (not_1_out, WE);
  Control_Logic_16_bit_CPU control_logic_16_bit_cpu_1 (
    .R_I(CLU_Input[3]), .SW_LW(CLU_Input[2]), .ALU_OP(CLU_Input[1:0]), .IMM_MUX(IMM_MUX),
    .SW(control_logic_16_bit_cpu_1_sw), .WE_MUX(WE_MUX), .RA2_MUX(RA2_MUX), .out_9(WE),
    .Data_In_MUX(Data_In_MUX), .LW(control_logic_16_bit_cpu_1_lw), .ALU_op_2(OP), .Func(Func));  // open: SLT
  // Probe on {Func, ram_1_data[2:0]}
  Multiplexer #(.width(3), .enable("false")) multiplexer_2 (
    .in0(ram_1_data[2:0]), .in1(ram_1_data[11:9]), .out(multiplexer_2_out), .sel(RA2_MUX));
  // Probe on multiplexer_3_out
  _8x16_bit_RF u_8x16_bit_rf_1 (
    .Data_In(multiplexer_3_out), .Write_Enable(multiplexer_1_out), .Clock(CLK),
    .Read_1_Data(n8x16_bit_rf_1_read_1_data), .Read_2_Data(Din), .Write_Addr(ram_1_data[11:9]),
    .Read_Addr_1(ram_1_data[8:6]), .Read_Addr_2(multiplexer_2_out));
  assign bit_extender_1_out = {{10{Func[2]}}, {Func, ram_1_data[2:0]}};  // Bit_Extender bit_extender_1
  Multiplexer #(.width(16), .enable("false")) multiplexer_3 (
    .in0(CPU_Op_Out), .in1(ram_2_data), .out(multiplexer_3_out), .sel(Data_In_MUX));
  Multiplexer #(.width(16), .enable("false")) multiplexer_4 (
    .in0(Din), .in1(bit_extender_1_out), .out(multiplexer_4_out), .sel(IMM_MUX));
  // Probe on multiplexer_4_out
  _16_bit_ALU u_16_bit_alu_1 (.A(n8x16_bit_rf_1_read_1_data), .B(multiplexer_4_out), .ALU_Out(CPU_Op_Out), .ALU_Op(OP));
  RAM #(.addrWidth(16), .dataWidth(16), .bus("separate")) ram_2 (
    .addr(CPU_Op_Out), .din(Din), .data(ram_2_data), .str(control_logic_16_bit_cpu_1_sw), .sel(1'b1),
    .clk(CLK), .ld(control_logic_16_bit_cpu_1_lw), .clr(1'b0));

  // Notes on the sheet:
  //   src2
  //   dest
  //   src1
  //   immed data
endmodule
